# Fritzing sketch botao (saved by Fritzing 0.9.3b)
breadboards: 1

parts:
  Componente1 = Arduino Uno (Rev3)
  R1 = Resistor [tolerance=±5% resistance=10k package=THT]
  S1 = Pushbutton [package="[THT]"]

nets:
  N1: Componente1.D10_PWM/SS, R1.Pin_0, S1.Pin_3, S1.Pin_4
  N2: Componente1.GND, R1.Pin_1
  N3: Componente1.5V, S1.Pin_1, S1.Pin_2
