# Fritzing sketch esquematico (saved by Fritzing 0.9.3b)
breadboards: 1

parts:
  U1 = LCD-16X2 [package=lcd-16x2]
  Componente1 = Arduino Uno (Rev3)
  U2 = POT [package=pot_mammoth]

nets:
  VSS: U1.VSS, U1.K, Componente1.GND, U2.E
  VDD: U1.VDD, U1.R_W, U1.A, Componente1.5V, U2.S
  N1: U1.VO, U2.A
  N2: U1.RS, Componente1.D12/MISO
  N3: U1.E, Componente1.D11_PWM/MOSI
  N4: U1.DB4, Componente1.D5_PWM
  N5: U1.DB5, Componente1.D4
  N6: U1.DB6, Componente1.D3_PWM
  N7: U1.DB7, Componente1.D2
