# Fritzing sketch keypad_4x4 (saved by Fritzing 0.9.3b)
breadboards: 1

parts:
  Part1 = Arduino Uno (Rev3)
  Matrix_keypad1 = KEYPAD 4x4
  R1 = Resistor [tolerance=±5% resistance=10k package="2010 [SMD]"]
  R2 = Resistor [tolerance=±5% resistance=10k package="2010 [SMD]"]
  R3 = Resistor [tolerance=±5% resistance=10k package="2010 [SMD]"]
  R4 = Resistor [tolerance=±5% resistance=10k package="2010 [SMD]"]

nets:
  N1: Part1.D8, Matrix_keypad1.col4
  N2: Part1.D9_PWM, Matrix_keypad1.col3
  N3: Part1.D10_PWM/SS, Matrix_keypad1.col2
  N4: Part1.D11_PWM/MOSI, Matrix_keypad1.col1
  N5: Part1.D4, Matrix_keypad1.row4, R1.Pin_0
  N6: Part1.D5_PWM, Matrix_keypad1.row3, R2.Pin_0
  N7: Part1.D6_PWM, Matrix_keypad1.row2, R4.Pin_0
  N8: Part1.D7, Matrix_keypad1.row1, R3.Pin_0
  N9: Part1.GND, R1.Pin_1, R2.Pin_1, R3.Pin_1, R4.Pin_1

custom parts:
  KEYPAD 4x4: Matrix keypad 16 buttons, 4 rows x 4 columns
