# Fritzing sketch leds_conduzidos (saved by Fritzing 0.9.3b)
breadboards: 1

parts:
  Componente1 = Arduino Uno (Rev3)
  R1 = Resistor [tolerance=±5% resistance=220 package=THT]
  R2 = Resistor [tolerance=±5% resistance=220 package=THT]
  R3 = Resistor [tolerance=±5% resistance=220 package=THT]
  R4 = Resistor [tolerance=±5% resistance=220 package=THT]
  R5 = Resistor [tolerance=±5% resistance=220 package=THT]
  R6 = Resistor [tolerance=±5% resistance=220 package=THT]
  R7 = Resistor [tolerance=±5% resistance=220 package=THT]
  R8 = Resistor [tolerance=±5% resistance=220 package=THT]
  LED1 = LED - 3mm [color="White (4500K)" package="3 mm [THT]"]
  LED2 = LED - 3mm [color="Red (633nm)" package="3 mm [THT]"]
  LED3 = LED - 3mm [color="Blue (505nm)" package="3 mm [THT]"]
  LED4 = LED - 3mm [color="Yellow (592nm)" package="3 mm [THT]"]
  LED5 = LED - 3mm [color="Green (570nm)" package="3 mm [THT]"]
  LED6 = LED - 3mm [color="Red (633nm)" package="3 mm [THT]"]
  LED8 = LED - 3mm [color="Green (560nm)" package="3 mm [THT]"]
  LED9 = LED - 3mm [color="Yellow (585nm)" package="3 mm [THT]"]

nets:
  N1: Componente1.D8, R3.Pin_0
  N2: Componente1.D9_PWM, R2.Pin_0
  N3: Componente1.D10_PWM/SS, R1.Pin_0
  N4: Componente1.GND, LED1.cathode, LED2.cathode, LED3.cathode, LED4.cathode, LED5.cathode, LED6.cathode, LED8.cathode, LED9.cathode
  N5: Componente1.D3_PWM, R8.Pin_0
  N6: Componente1.D4, R7.Pin_0
  N7: Componente1.D5_PWM, R6.Pin_0
  N8: Componente1.D6_PWM, R5.Pin_0
  N9: Componente1.D7, R4.Pin_0
  N10: R1.Pin_1, LED1.anode
  N11: R2.Pin_1, LED2.anode
  N12: R3.Pin_1, LED3.anode
  N13: R4.Pin_1, LED4.anode
  N14: R5.Pin_1, LED5.anode
  N15: R6.Pin_1, LED6.anode
  N16: R7.Pin_1, LED9.anode
  N17: R8.Pin_1, LED8.anode
